// Logisim project ALU.circ as structural Verilog
module ArithmeticUnit (
  input  in_1,
  input  in_2,
  input  in_3,
  input  in_4,
  input  in_5,
  input  in_6,
  input  in_7,
  input  in_8,
  input  in_9,
  output out_10,
  output out_11,
  output out_12,
  output out_13,
  output out_14
);

  wire fulladder_1_carry, fulladder_2_carry, fulladder_3_carry, xor_1_out, xor_2_out, xor_3_out, xor_4_out;

  xor xor_1 (xor_1_out, in_9, in_5);
  xor xor_2 (xor_2_out, in_6, in_9);
  FullAdder fulladder_1 (.A(in_9), .B(in_1), .C(xor_1_out), .SUM(out_10), .CARRY(fulladder_1_carry));
  xor xor_3 (xor_3_out, in_7, in_9);
  FullAdder fulladder_2 (.A(fulladder_1_carry), .B(in_2), .C(xor_2_out), .SUM(out_11), .CARRY(fulladder_2_carry));
  xor xor_4 (xor_4_out, in_8, in_9);
  FullAdder fulladder_3 (.A(fulladder_2_carry), .B(in_3), .C(xor_3_out), .SUM(out_12), .CARRY(fulladder_3_carry));
  FullAdder fulladder_4 (.A(fulladder_3_carry), .B(in_4), .C(xor_4_out), .SUM(out_13), .CARRY(out_14));
endmodule

// FA
module FullAdder (
  input  A,
  input  B,
  input  C,
  output SUM,
  output CARRY
);

  wire and_1_out, and_2_out, xor_1_out;

  xor xor_1 (xor_1_out, A, B);
  and and_1 (and_1_out, A, B);
  and and_2 (and_2_out, xor_1_out, C);
  xor xor_2 (SUM, xor_1_out, C);
  or or_1 (CARRY, and_2_out, and_1_out);
endmodule
