// Logisim project AU1940151_Purvam-Sheth_RAM.circ as structural Verilog: 4 circuits, main circuit main
module main (
  input  Selection,
  input  Clk,
  input  Input,
  input  Read_Write,
  output Q,
  output Q_prime
);

  D_Flip_Flop d_flip_flop_1 (
    .Clk(Clk), .Input(Input), .Selection(Selection), .Read_Write(Read_Write), .Q(Q), .Q_prime(Q_prime));

  // Notes on the sheet:
  //   For read operation -> 0
  //   D-Flip Flop component
  //   For write operation -> 1
  //   Purvam Sheth
  //   AU1940151
endmodule

module D_Flip_Flop (
  input  Selection,
  input  Clk,
  input  Input,
  input  Read_Write,
  output Q,
  output Q_prime
);

  wire and_1_out, and_2_out, nor_1_out, not_1_out, not_2_out;

  not not_1 (not_1_out, Input);
  not not_2 (not_2_out, Read_Write);
  and and_1 (and_1_out, Selection, not_1_out, not_2_out, Clk);
  and and_2 (and_2_out, Clk, not_2_out, Input, Selection);
  nor nor_1 (nor_1_out, and_1_out, Q_prime);
  nor nor_2 (Q_prime, nor_1_out, and_2_out);
  and and_3 (Q, Selection, nor_1_out, Read_Write);

  // Notes on the sheet:
  //   For read operation -> 0
  //   For write operation -> 1
  //   AU1940151
  //   Purvam Sheth
endmodule

// RAM 32*4
module RAM__32_4__Internal_Circuitry (
  input  i3,
  input  i2,
  input  i1,
  input  i0,
  input  [4:0] in_5,
  input  in_6,
  input  Read_Write,
  output o3,
  output o1,
  output o0,
  output o2
);

  wire decoder_1_out0, decoder_1_out1, decoder_1_out2, decoder_1_out3, decoder_1_out4, decoder_1_out5,
       decoder_1_out6, decoder_1_out7, decoder_1_out8, decoder_1_out9, decoder_1_out10, decoder_1_out11,
       decoder_1_out12, decoder_1_out13, decoder_1_out14, decoder_1_out15, decoder_1_out16, decoder_1_out17,
       decoder_1_out18, decoder_1_out19, decoder_1_out20, decoder_1_out21, decoder_1_out22, decoder_1_out23,
       decoder_1_out24, decoder_1_out25, decoder_1_out26, decoder_1_out27, decoder_1_out28, decoder_1_out29,
       decoder_1_out30, decoder_1_out31, main_1_q, main_2_q, main_3_q, main_4_q, main_5_q, main_6_q,
       main_7_q, main_8_q, main_9_q, main_10_q, main_11_q, main_12_q, main_13_q, main_14_q, main_15_q,
       main_16_q, main_17_q, main_18_q, main_19_q, main_20_q, main_21_q, main_22_q, main_23_q, main_24_q,
       main_25_q, main_26_q, main_27_q, main_28_q, main_29_q, main_30_q, main_31_q, main_32_q, main_33_q,
       main_34_q, main_35_q, main_36_q, main_37_q, main_38_q, main_39_q, main_40_q, main_41_q, main_42_q,
       main_43_q, main_44_q, main_45_q, main_46_q, main_47_q, main_48_q, main_49_q, main_50_q, main_51_q,
       main_52_q, main_53_q, main_54_q, main_55_q, main_56_q, main_57_q, main_58_q, main_59_q, main_60_q,
       main_61_q, main_62_q, main_63_q, main_64_q, main_65_q, main_66_q, main_67_q, main_68_q, main_69_q,
       main_70_q, main_71_q, main_72_q, main_73_q, main_74_q, main_75_q, main_76_q, main_77_q, main_78_q,
       main_79_q, main_80_q, main_81_q, main_82_q, main_83_q, main_84_q, main_85_q, main_86_q, main_87_q,
       main_88_q, main_89_q, main_90_q, main_91_q, main_92_q, main_93_q, main_94_q, main_95_q, main_96_q,
       main_97_q, main_98_q, main_99_q, main_100_q, main_101_q, main_102_q, main_103_q, main_104_q,
       main_105_q, main_106_q, main_107_q, main_108_q, main_109_q, main_110_q, main_111_q, main_112_q,
       main_113_q, main_114_q, main_115_q, main_116_q, main_117_q, main_118_q, main_119_q, main_120_q,
       main_121_q, main_122_q, main_123_q, main_124_q, main_125_q, main_126_q, main_127_q, main_128_q;

  Decoder #(.select(5)) decoder_1 (
    .out0(decoder_1_out0), .out1(decoder_1_out1), .out2(decoder_1_out2), .out3(decoder_1_out3),
    .out4(decoder_1_out4), .out5(decoder_1_out5), .out6(decoder_1_out6), .out7(decoder_1_out7),
    .out8(decoder_1_out8), .out9(decoder_1_out9), .out10(decoder_1_out10), .out11(decoder_1_out11),
    .out12(decoder_1_out12), .out13(decoder_1_out13), .out14(decoder_1_out14), .out15(decoder_1_out15),
    .out16(decoder_1_out16), .out17(decoder_1_out17), .out18(decoder_1_out18), .out19(decoder_1_out19),
    .out20(decoder_1_out20), .out21(decoder_1_out21), .out22(decoder_1_out22), .out23(decoder_1_out23),
    .out24(decoder_1_out24), .out25(decoder_1_out25), .out26(decoder_1_out26), .out27(decoder_1_out27),
    .out28(decoder_1_out28), .out29(decoder_1_out29), .out30(decoder_1_out30), .out31(decoder_1_out31),
    .sel(in_5), .en(1'b1));
  main main_1 (
    .Q(main_1_q), .Selection(decoder_1_out0), .Read_Write(Read_Write), .Input(i3), .Clk(in_6));  // open: Q_prime
  main main_2 (
    .Q(main_2_q), .Selection(decoder_1_out1), .Read_Write(Read_Write), .Input(i3), .Clk(in_6));  // open: Q_prime
  main main_3 (
    .Q(main_3_q), .Selection(decoder_1_out2), .Read_Write(Read_Write), .Input(i3), .Clk(in_6));  // open: Q_prime
  main main_4 (
    .Q(main_4_q), .Selection(decoder_1_out3), .Read_Write(Read_Write), .Input(i3), .Clk(in_6));  // open: Q_prime
  main main_5 (
    .Q(main_5_q), .Selection(decoder_1_out4), .Read_Write(Read_Write), .Input(i3), .Clk(in_6));  // open: Q_prime
  main main_6 (
    .Q(main_6_q), .Selection(decoder_1_out5), .Read_Write(Read_Write), .Input(i3), .Clk(in_6));  // open: Q_prime
  main main_7 (
    .Q(main_7_q), .Selection(decoder_1_out6), .Read_Write(Read_Write), .Input(i3), .Clk(in_6));  // open: Q_prime
  main main_8 (
    .Q(main_8_q), .Selection(decoder_1_out7), .Read_Write(Read_Write), .Input(i3), .Clk(in_6));  // open: Q_prime
  main main_9 (
    .Q(main_9_q), .Selection(decoder_1_out8), .Read_Write(Read_Write), .Input(i3), .Clk(in_6));  // open: Q_prime
  main main_10 (
    .Q(main_10_q), .Selection(decoder_1_out9), .Read_Write(Read_Write), .Input(i3), .Clk(in_6));  // open: Q_prime
  main main_11 (
    .Q(main_11_q), .Selection(decoder_1_out10), .Read_Write(Read_Write), .Input(i3), .Clk(in_6));  // open: Q_prime
  main main_12 (
    .Q(main_12_q), .Selection(decoder_1_out11), .Read_Write(Read_Write), .Input(i3), .Clk(in_6));  // open: Q_prime
  main main_13 (
    .Q(main_13_q), .Selection(decoder_1_out12), .Read_Write(Read_Write), .Input(i3), .Clk(in_6));  // open: Q_prime
  main main_14 (
    .Q(main_14_q), .Selection(decoder_1_out13), .Read_Write(Read_Write), .Input(i3), .Clk(in_6));  // open: Q_prime
  main main_15 (
    .Q(main_15_q), .Selection(decoder_1_out14), .Read_Write(Read_Write), .Input(i3), .Clk(in_6));  // open: Q_prime
  main main_16 (
    .Q(main_16_q), .Selection(decoder_1_out15), .Read_Write(Read_Write), .Input(i3), .Clk(in_6));  // open: Q_prime
  main main_17 (
    .Q(main_17_q), .Selection(decoder_1_out16), .Read_Write(Read_Write), .Input(i3), .Clk(in_6));  // open: Q_prime
  main main_18 (
    .Q(main_18_q), .Selection(decoder_1_out17), .Read_Write(Read_Write), .Input(i3), .Clk(in_6));  // open: Q_prime
  main main_19 (
    .Q(main_19_q), .Selection(decoder_1_out18), .Read_Write(Read_Write), .Input(i3), .Clk(in_6));  // open: Q_prime
  main main_20 (
    .Q(main_20_q), .Selection(decoder_1_out19), .Read_Write(Read_Write), .Input(i3), .Clk(in_6));  // open: Q_prime
  main main_21 (
    .Q(main_21_q), .Selection(decoder_1_out20), .Read_Write(Read_Write), .Input(i3), .Clk(in_6));  // open: Q_prime
  main main_22 (
    .Q(main_22_q), .Selection(decoder_1_out21), .Read_Write(Read_Write), .Input(i3), .Clk(in_6));  // open: Q_prime
  main main_23 (
    .Q(main_23_q), .Selection(decoder_1_out22), .Read_Write(Read_Write), .Input(i3), .Clk(in_6));  // open: Q_prime
  main main_24 (
    .Q(main_24_q), .Selection(decoder_1_out23), .Read_Write(Read_Write), .Input(i3), .Clk(in_6));  // open: Q_prime
  main main_25 (
    .Q(main_25_q), .Selection(decoder_1_out24), .Read_Write(Read_Write), .Input(i3), .Clk(in_6));  // open: Q_prime
  main main_26 (
    .Q(main_26_q), .Selection(decoder_1_out25), .Read_Write(Read_Write), .Input(i3), .Clk(in_6));  // open: Q_prime
  main main_27 (
    .Q(main_27_q), .Selection(decoder_1_out26), .Read_Write(Read_Write), .Input(i3), .Clk(in_6));  // open: Q_prime
  main main_28 (
    .Q(main_28_q), .Selection(decoder_1_out27), .Read_Write(Read_Write), .Input(i3), .Clk(in_6));  // open: Q_prime
  main main_29 (
    .Q(main_29_q), .Selection(decoder_1_out28), .Read_Write(Read_Write), .Input(i3), .Clk(in_6));  // open: Q_prime
  main main_30 (
    .Q(main_30_q), .Selection(decoder_1_out29), .Read_Write(Read_Write), .Input(i3), .Clk(in_6));  // open: Q_prime
  main main_31 (
    .Q(main_31_q), .Selection(decoder_1_out30), .Read_Write(Read_Write), .Input(i3), .Clk(in_6));  // open: Q_prime
  main main_32 (
    .Q(main_32_q), .Selection(decoder_1_out31), .Read_Write(Read_Write), .Input(i3), .Clk(in_6));  // open: Q_prime
  or or_1 (o3, main_1_q, main_2_q, main_3_q, main_4_q, main_5_q, main_6_q, main_7_q, main_8_q, main_9_q, main_10_q, main_11_q, main_12_q, main_13_q, main_14_q, main_15_q, main_16_q, main_17_q, main_18_q, main_19_q, main_20_q, main_21_q, main_22_q, main_23_q, main_24_q, main_25_q, main_26_q, main_27_q, main_28_q, main_29_q, main_30_q, main_31_q, main_32_q);
  main main_33 (
    .Q(main_33_q), .Selection(decoder_1_out0), .Read_Write(Read_Write), .Input(i2), .Clk(in_6));  // open: Q_prime
  main main_34 (
    .Q(main_34_q), .Selection(decoder_1_out1), .Read_Write(Read_Write), .Input(i2), .Clk(in_6));  // open: Q_prime
  main main_35 (
    .Q(main_35_q), .Selection(decoder_1_out2), .Read_Write(Read_Write), .Input(i2), .Clk(in_6));  // open: Q_prime
  main main_36 (
    .Q(main_36_q), .Selection(decoder_1_out3), .Read_Write(Read_Write), .Input(i2), .Clk(in_6));  // open: Q_prime
  main main_37 (
    .Q(main_37_q), .Selection(decoder_1_out4), .Read_Write(Read_Write), .Input(i2), .Clk(in_6));  // open: Q_prime
  main main_38 (
    .Q(main_38_q), .Selection(decoder_1_out5), .Read_Write(Read_Write), .Input(i2), .Clk(in_6));  // open: Q_prime
  main main_39 (
    .Q(main_39_q), .Selection(decoder_1_out6), .Read_Write(Read_Write), .Input(i2), .Clk(in_6));  // open: Q_prime
  main main_40 (
    .Q(main_40_q), .Selection(decoder_1_out7), .Read_Write(Read_Write), .Input(i2), .Clk(in_6));  // open: Q_prime
  main main_41 (
    .Q(main_41_q), .Selection(decoder_1_out8), .Read_Write(Read_Write), .Input(i2), .Clk(in_6));  // open: Q_prime
  main main_42 (
    .Q(main_42_q), .Selection(decoder_1_out9), .Read_Write(Read_Write), .Input(i2), .Clk(in_6));  // open: Q_prime
  main main_43 (
    .Q(main_43_q), .Selection(decoder_1_out10), .Read_Write(Read_Write), .Input(i2), .Clk(in_6));  // open: Q_prime
  main main_44 (
    .Q(main_44_q), .Selection(decoder_1_out11), .Read_Write(Read_Write), .Input(i2), .Clk(in_6));  // open: Q_prime
  main main_45 (
    .Q(main_45_q), .Selection(decoder_1_out12), .Read_Write(Read_Write), .Input(i2), .Clk(in_6));  // open: Q_prime
  main main_46 (
    .Q(main_46_q), .Selection(decoder_1_out13), .Read_Write(Read_Write), .Input(i2), .Clk(in_6));  // open: Q_prime
  main main_47 (
    .Q(main_47_q), .Selection(decoder_1_out14), .Read_Write(Read_Write), .Input(i2), .Clk(in_6));  // open: Q_prime
  main main_48 (
    .Q(main_48_q), .Selection(decoder_1_out15), .Read_Write(Read_Write), .Input(i2), .Clk(in_6));  // open: Q_prime
  main main_49 (
    .Q(main_49_q), .Selection(decoder_1_out16), .Read_Write(Read_Write), .Input(i2), .Clk(in_6));  // open: Q_prime
  main main_50 (
    .Q(main_50_q), .Selection(decoder_1_out17), .Read_Write(Read_Write), .Input(i2), .Clk(in_6));  // open: Q_prime
  main main_51 (
    .Q(main_51_q), .Selection(decoder_1_out18), .Read_Write(Read_Write), .Input(i2), .Clk(in_6));  // open: Q_prime
  main main_52 (
    .Q(main_52_q), .Selection(decoder_1_out19), .Read_Write(Read_Write), .Input(i2), .Clk(in_6));  // open: Q_prime
  main main_53 (
    .Q(main_53_q), .Selection(decoder_1_out20), .Read_Write(Read_Write), .Input(i2), .Clk(in_6));  // open: Q_prime
  main main_54 (
    .Q(main_54_q), .Selection(decoder_1_out21), .Read_Write(Read_Write), .Input(i2), .Clk(in_6));  // open: Q_prime
  main main_55 (
    .Q(main_55_q), .Selection(decoder_1_out22), .Read_Write(Read_Write), .Input(i2), .Clk(in_6));  // open: Q_prime
  main main_56 (
    .Q(main_56_q), .Selection(decoder_1_out23), .Read_Write(Read_Write), .Input(i2), .Clk(in_6));  // open: Q_prime
  main main_57 (
    .Q(main_57_q), .Selection(decoder_1_out24), .Read_Write(Read_Write), .Input(i2), .Clk(in_6));  // open: Q_prime
  main main_58 (
    .Q(main_58_q), .Selection(decoder_1_out25), .Read_Write(Read_Write), .Input(i2), .Clk(in_6));  // open: Q_prime
  main main_59 (
    .Q(main_59_q), .Selection(decoder_1_out26), .Read_Write(Read_Write), .Input(i2), .Clk(in_6));  // open: Q_prime
  main main_60 (
    .Q(main_60_q), .Selection(decoder_1_out27), .Read_Write(Read_Write), .Input(i2), .Clk(in_6));  // open: Q_prime
  main main_61 (
    .Q(main_61_q), .Selection(decoder_1_out28), .Read_Write(Read_Write), .Input(i2), .Clk(in_6));  // open: Q_prime
  main main_62 (
    .Q(main_62_q), .Selection(decoder_1_out29), .Read_Write(Read_Write), .Input(i2), .Clk(in_6));  // open: Q_prime
  main main_63 (
    .Q(main_63_q), .Selection(decoder_1_out30), .Read_Write(Read_Write), .Input(i2), .Clk(in_6));  // open: Q_prime
  main main_64 (
    .Q(main_64_q), .Selection(decoder_1_out31), .Read_Write(Read_Write), .Input(i2), .Clk(in_6));  // open: Q_prime
  or or_2 (o2, main_33_q, main_34_q, main_35_q, main_36_q, main_37_q, main_38_q, main_39_q, main_40_q, main_41_q, main_42_q, main_43_q, main_44_q, main_45_q, main_46_q, main_47_q, main_48_q, main_49_q, main_50_q, main_51_q, main_52_q, main_53_q, main_54_q, main_55_q, main_56_q, main_57_q, main_58_q, main_59_q, main_60_q, main_61_q, main_62_q, main_63_q, main_64_q);
  main main_65 (
    .Q(main_65_q), .Selection(decoder_1_out0), .Read_Write(Read_Write), .Input(i1), .Clk(in_6));  // open: Q_prime
  main main_66 (
    .Q(main_66_q), .Selection(decoder_1_out1), .Read_Write(Read_Write), .Input(i1), .Clk(in_6));  // open: Q_prime
  main main_67 (
    .Q(main_67_q), .Selection(decoder_1_out2), .Read_Write(Read_Write), .Input(i1), .Clk(in_6));  // open: Q_prime
  main main_68 (
    .Q(main_68_q), .Selection(decoder_1_out3), .Read_Write(Read_Write), .Input(i1), .Clk(in_6));  // open: Q_prime
  main main_69 (
    .Q(main_69_q), .Selection(decoder_1_out4), .Read_Write(Read_Write), .Input(i1), .Clk(in_6));  // open: Q_prime
  main main_70 (
    .Q(main_70_q), .Selection(decoder_1_out5), .Read_Write(Read_Write), .Input(i1), .Clk(in_6));  // open: Q_prime
  main main_71 (
    .Q(main_71_q), .Selection(decoder_1_out6), .Read_Write(Read_Write), .Input(i1), .Clk(in_6));  // open: Q_prime
  main main_72 (
    .Q(main_72_q), .Selection(decoder_1_out7), .Read_Write(Read_Write), .Input(i1), .Clk(in_6));  // open: Q_prime
  main main_73 (
    .Q(main_73_q), .Selection(decoder_1_out8), .Read_Write(Read_Write), .Input(i1), .Clk(in_6));  // open: Q_prime
  main main_74 (
    .Q(main_74_q), .Selection(decoder_1_out9), .Read_Write(Read_Write), .Input(i1), .Clk(in_6));  // open: Q_prime
  main main_75 (
    .Q(main_75_q), .Selection(decoder_1_out10), .Read_Write(Read_Write), .Input(i1), .Clk(in_6));  // open: Q_prime
  main main_76 (
    .Q(main_76_q), .Selection(decoder_1_out11), .Read_Write(Read_Write), .Input(i1), .Clk(in_6));  // open: Q_prime
  main main_77 (
    .Q(main_77_q), .Selection(decoder_1_out12), .Read_Write(Read_Write), .Input(i1), .Clk(in_6));  // open: Q_prime
  main main_78 (
    .Q(main_78_q), .Selection(decoder_1_out13), .Read_Write(Read_Write), .Input(i1), .Clk(in_6));  // open: Q_prime
  main main_79 (
    .Q(main_79_q), .Selection(decoder_1_out14), .Read_Write(Read_Write), .Input(i1), .Clk(in_6));  // open: Q_prime
  main main_80 (
    .Q(main_80_q), .Selection(decoder_1_out15), .Read_Write(Read_Write), .Input(i1), .Clk(in_6));  // open: Q_prime
  main main_81 (
    .Q(main_81_q), .Selection(decoder_1_out16), .Read_Write(Read_Write), .Input(i1), .Clk(in_6));  // open: Q_prime
  main main_82 (
    .Q(main_82_q), .Selection(decoder_1_out17), .Read_Write(Read_Write), .Input(i1), .Clk(in_6));  // open: Q_prime
  main main_83 (
    .Q(main_83_q), .Selection(decoder_1_out18), .Read_Write(Read_Write), .Input(i1), .Clk(in_6));  // open: Q_prime
  main main_84 (
    .Q(main_84_q), .Selection(decoder_1_out19), .Read_Write(Read_Write), .Input(i1), .Clk(in_6));  // open: Q_prime
  main main_85 (
    .Q(main_85_q), .Selection(decoder_1_out20), .Read_Write(Read_Write), .Input(i1), .Clk(in_6));  // open: Q_prime
  main main_86 (
    .Q(main_86_q), .Selection(decoder_1_out21), .Read_Write(Read_Write), .Input(i1), .Clk(in_6));  // open: Q_prime
  main main_87 (
    .Q(main_87_q), .Selection(decoder_1_out22), .Read_Write(Read_Write), .Input(i1), .Clk(in_6));  // open: Q_prime
  main main_88 (
    .Q(main_88_q), .Selection(decoder_1_out23), .Read_Write(Read_Write), .Input(i1), .Clk(in_6));  // open: Q_prime
  main main_89 (
    .Q(main_89_q), .Selection(decoder_1_out24), .Read_Write(Read_Write), .Input(i1), .Clk(in_6));  // open: Q_prime
  main main_90 (
    .Q(main_90_q), .Selection(decoder_1_out25), .Read_Write(Read_Write), .Input(i1), .Clk(in_6));  // open: Q_prime
  main main_91 (
    .Q(main_91_q), .Selection(decoder_1_out26), .Read_Write(Read_Write), .Input(i1), .Clk(in_6));  // open: Q_prime
  main main_92 (
    .Q(main_92_q), .Selection(decoder_1_out27), .Read_Write(Read_Write), .Input(i1), .Clk(in_6));  // open: Q_prime
  main main_93 (
    .Q(main_93_q), .Selection(decoder_1_out28), .Read_Write(Read_Write), .Input(i1), .Clk(in_6));  // open: Q_prime
  main main_94 (
    .Q(main_94_q), .Selection(decoder_1_out29), .Read_Write(Read_Write), .Input(i1), .Clk(in_6));  // open: Q_prime
  main main_95 (
    .Q(main_95_q), .Selection(decoder_1_out30), .Read_Write(Read_Write), .Input(i1), .Clk(in_6));  // open: Q_prime
  main main_96 (
    .Q(main_96_q), .Selection(decoder_1_out31), .Read_Write(Read_Write), .Input(i1), .Clk(in_6));  // open: Q_prime
  or or_3 (o1, main_65_q, main_66_q, main_67_q, main_68_q, main_69_q, main_70_q, main_71_q, main_72_q, main_73_q, main_74_q, main_75_q, main_76_q, main_77_q, main_78_q, main_79_q, main_80_q, main_81_q, main_82_q, main_83_q, main_84_q, main_85_q, main_86_q, main_87_q, main_88_q, main_89_q, main_90_q, main_91_q, main_92_q, main_93_q, main_94_q, main_95_q, main_96_q);
  main main_97 (
    .Q(main_97_q), .Selection(decoder_1_out0), .Read_Write(Read_Write), .Input(i0), .Clk(in_6));  // open: Q_prime
  main main_98 (
    .Q(main_98_q), .Selection(decoder_1_out1), .Read_Write(Read_Write), .Input(i0), .Clk(in_6));  // open: Q_prime
  main main_99 (
    .Q(main_99_q), .Selection(decoder_1_out2), .Read_Write(Read_Write), .Input(i0), .Clk(in_6));  // open: Q_prime
  main main_100 (
    .Q(main_100_q), .Selection(decoder_1_out3), .Read_Write(Read_Write), .Input(i0), .Clk(in_6));  // open: Q_prime
  main main_101 (
    .Q(main_101_q), .Selection(decoder_1_out4), .Read_Write(Read_Write), .Input(i0), .Clk(in_6));  // open: Q_prime
  main main_102 (
    .Q(main_102_q), .Selection(decoder_1_out5), .Read_Write(Read_Write), .Input(i0), .Clk(in_6));  // open: Q_prime
  main main_103 (
    .Q(main_103_q), .Selection(decoder_1_out6), .Read_Write(Read_Write), .Input(i0), .Clk(in_6));  // open: Q_prime
  main main_104 (
    .Q(main_104_q), .Selection(decoder_1_out7), .Read_Write(Read_Write), .Input(i0), .Clk(in_6));  // open: Q_prime
  main main_105 (
    .Q(main_105_q), .Selection(decoder_1_out8), .Read_Write(Read_Write), .Input(i0), .Clk(in_6));  // open: Q_prime
  main main_106 (
    .Q(main_106_q), .Selection(decoder_1_out9), .Read_Write(Read_Write), .Input(i0), .Clk(in_6));  // open: Q_prime
  main main_107 (
    .Q(main_107_q), .Selection(decoder_1_out10), .Read_Write(Read_Write), .Input(i0), .Clk(in_6));  // open: Q_prime
  main main_108 (
    .Q(main_108_q), .Selection(decoder_1_out11), .Read_Write(Read_Write), .Input(i0), .Clk(in_6));  // open: Q_prime
  main main_109 (
    .Q(main_109_q), .Selection(decoder_1_out12), .Read_Write(Read_Write), .Input(i0), .Clk(in_6));  // open: Q_prime
  main main_110 (
    .Q(main_110_q), .Selection(decoder_1_out13), .Read_Write(Read_Write), .Input(i0), .Clk(in_6));  // open: Q_prime
  main main_111 (
    .Q(main_111_q), .Selection(decoder_1_out14), .Read_Write(Read_Write), .Input(i0), .Clk(in_6));  // open: Q_prime
  main main_112 (
    .Q(main_112_q), .Selection(decoder_1_out15), .Read_Write(Read_Write), .Input(i0), .Clk(in_6));  // open: Q_prime
  main main_113 (
    .Q(main_113_q), .Selection(decoder_1_out16), .Read_Write(Read_Write), .Input(i0), .Clk(in_6));  // open: Q_prime
  main main_114 (
    .Q(main_114_q), .Selection(decoder_1_out17), .Read_Write(Read_Write), .Input(i0), .Clk(in_6));  // open: Q_prime
  main main_115 (
    .Q(main_115_q), .Selection(decoder_1_out18), .Read_Write(Read_Write), .Input(i0), .Clk(in_6));  // open: Q_prime
  main main_116 (
    .Q(main_116_q), .Selection(decoder_1_out19), .Read_Write(Read_Write), .Input(i0), .Clk(in_6));  // open: Q_prime
  main main_117 (
    .Q(main_117_q), .Selection(decoder_1_out20), .Read_Write(Read_Write), .Input(i0), .Clk(in_6));  // open: Q_prime
  main main_118 (
    .Q(main_118_q), .Selection(decoder_1_out21), .Read_Write(Read_Write), .Input(i0), .Clk(in_6));  // open: Q_prime
  main main_119 (
    .Q(main_119_q), .Selection(decoder_1_out22), .Read_Write(Read_Write), .Input(i0), .Clk(in_6));  // open: Q_prime
  main main_120 (
    .Q(main_120_q), .Selection(decoder_1_out23), .Read_Write(Read_Write), .Input(i0), .Clk(in_6));  // open: Q_prime
  main main_121 (
    .Q(main_121_q), .Selection(decoder_1_out24), .Read_Write(Read_Write), .Input(i0), .Clk(in_6));  // open: Q_prime
  main main_122 (
    .Q(main_122_q), .Selection(decoder_1_out25), .Read_Write(Read_Write), .Input(i0), .Clk(in_6));  // open: Q_prime
  main main_123 (
    .Q(main_123_q), .Selection(decoder_1_out26), .Read_Write(Read_Write), .Input(i0), .Clk(in_6));  // open: Q_prime
  main main_124 (
    .Q(main_124_q), .Selection(decoder_1_out27), .Read_Write(Read_Write), .Input(i0), .Clk(in_6));  // open: Q_prime
  main main_125 (
    .Q(main_125_q), .Selection(decoder_1_out28), .Read_Write(Read_Write), .Input(i0), .Clk(in_6));  // open: Q_prime
  main main_126 (
    .Q(main_126_q), .Selection(decoder_1_out29), .Read_Write(Read_Write), .Input(i0), .Clk(in_6));  // open: Q_prime
  main main_127 (
    .Q(main_127_q), .Selection(decoder_1_out30), .Read_Write(Read_Write), .Input(i0), .Clk(in_6));  // open: Q_prime
  main main_128 (
    .Q(main_128_q), .Selection(decoder_1_out31), .Read_Write(Read_Write), .Input(i0), .Clk(in_6));  // open: Q_prime
  or or_4 (o0, main_97_q, main_98_q, main_99_q, main_100_q, main_101_q, main_102_q, main_103_q, main_104_q, main_105_q, main_106_q, main_107_q, main_108_q, main_109_q, main_110_q, main_111_q, main_112_q, main_113_q, main_114_q, main_115_q, main_116_q, main_117_q, main_118_q, main_119_q, main_120_q, main_121_q, main_122_q, main_123_q, main_124_q, main_125_q, main_126_q, main_127_q, main_128_q);

  // Notes on the sheet:
  //   For read operation -> 0
  //   For write operation -> 1
endmodule

module RAM__32_4__Main_Circuitry (
  input  i3,
  input  i2,
  input  i1,
  input  i0,
  input  [4:0] Row_selection,
  input  Read_Write,
  output o3,
  output _02,
  output o1,
  output o0
);

  wire Clk_out;

  Clock Clk (.out(Clk_out));
  RAM__32_4__Internal_Circuitry ram_32_4_internal_circuitry_1 (
    .in_5(Row_selection), .i3(i3), .i2(i2), .i1(i1), .i0(i0), .Read_Write(Read_Write), .o3(o3), .o2(_02),
    .o1(o1), .o0(o0), .in_6(Clk_out));

  // Notes on the sheet:
  //   Purvam Sheth
  //   AU1940151
  //   For read operation -> 0
  //   For write operation -> 1
endmodule
